// Logisim project finalCircuit.circ as structural Verilog: 7 circuits, main circuit main
module main (
);

  wire bcd_to_7_segment_decoder_3_p1, binary_to_bcd_converter_1_p2, binary_to_bcd_converter_1_p4,
       ClearScreen, CLK_out, Halt, MemWriteEn, MOVE_DOWN_out, MOVE_UP_out, not_1_out, not_2_out, or_1_out,
       RESET_out, START_GAME_out, VRAMHoldEn, VRAMWriteEn;
  wire [3:0] controlled_buffer_1_out, portio_1_p3;
  wire [4:0] AddressBusOut, counter_1_q, CurrentAddress, register_1_q;
  wire [7:5] cpu_1_controlbus;
  wire [8:0] DataBusOut, ram_1_dout, Score;
  wire [31:0] ColumnData, PlayerYPos, vram_1_col1, vram_1_col2, vram_1_col3, vram_1_col4, vram_1_col5,
       vram_1_col6, vram_1_col7, vram_1_col8, vram_1_col9, vram_1_col10, vram_1_col11, vram_1_col12,
       vram_1_col13, vram_1_col14, vram_1_col15, vram_1_col16, vram_1_col17, vram_1_col18, vram_1_col19,
       vram_1_col20, vram_1_col21, vram_1_col22, vram_1_col23, vram_1_col24, vram_1_col25, vram_1_col26,
       vram_1_col27, vram_1_col28, vram_1_col29, vram_1_col30, vram_1_col31, vram_1_col32;

  Clock CLK (.out(CLK_out));
  Counter #(.max('h1f), .width(5)) counter_1 (.clk(CLK_out), .Q(counter_1_q));  // open: clr, load, up, count, D, carry
  Register #(.width(5)) register_1 (.D(CurrentAddress), .clk(CLK_out), .Q(register_1_q));  // open: en, clr
  Subtractor #(.width(5)) subtractor_1 (.a({5{1'b1}}), .b(counter_1_q), .out(CurrentAddress));  // open: bin, bout
  // Probe on ColumnData
  Button START_GAME (.out(START_GAME_out));
  Button MOVE_UP (.out(MOVE_UP_out));
  Button MOVE_DOWN (.out(MOVE_DOWN_out));
  assign controlled_buffer_1_out = START_GAME_out ? 4'b0001 : 4'bz;  // Controlled_Buffer controlled_buffer_1
  assign controlled_buffer_1_out = MOVE_UP_out ? 4'b0010 : 4'bz;  // Controlled_Buffer controlled_buffer_2
  assign controlled_buffer_1_out = MOVE_DOWN_out ? 4'b0011 : 4'bz;  // Controlled_Buffer controlled_buffer_3
  not not_1 (not_1_out, or_1_out);
  assign controlled_buffer_1_out = not_1_out ? 4'b0100 : 4'bz;  // Controlled_Buffer controlled_buffer_4
  or or_1 (or_1_out, START_GAME_out, MOVE_UP_out, MOVE_DOWN_out);
  // PortIO #(.number(4)) portio_1: pin names not known; wires that end beside it: 1'b1, controlled_buffer_1_out, portio_1_p3
  DotMatrix #(.matrixcols(3), .matrixrows(32)) dotmatrix_1 (.col0(PlayerYPos), .col1(PlayerYPos), .col2(PlayerYPos));
  DotMatrix #(.matrixcols(32), .matrixrows(32)) dotmatrix_2 (
    .col0(vram_1_col1), .col1(vram_1_col2), .col2(vram_1_col3), .col3(vram_1_col4), .col4(vram_1_col5),
    .col5(vram_1_col6), .col6(vram_1_col7), .col7(vram_1_col8), .col8(vram_1_col9), .col9(vram_1_col10),
    .col10(vram_1_col11), .col11(vram_1_col12), .col12(vram_1_col13), .col13(vram_1_col14),
    .col14(vram_1_col15), .col15(vram_1_col16), .col16(vram_1_col17), .col17(vram_1_col18),
    .col18(vram_1_col19), .col19(vram_1_col20), .col20(vram_1_col21), .col21(vram_1_col22),
    .col22(vram_1_col23), .col23(vram_1_col24), .col24(vram_1_col25), .col25(vram_1_col26),
    .col26(vram_1_col27), .col27(vram_1_col28), .col28(vram_1_col29), .col29(vram_1_col30),
    .col30(vram_1_col31), .col31(vram_1_col32));
  VRAM vram_1 (
    .AddressBus(register_1_q), .VRAMDataBus(ColumnData), .WriteEnable(VRAMHoldEn), .CLK(CLK_out),
    .Col1(vram_1_col1), .Col2(vram_1_col2), .Col3(vram_1_col3), .Col4(vram_1_col4), .Col5(vram_1_col5),
    .Col6(vram_1_col6), .Col7(vram_1_col7), .Col8(vram_1_col8), .Col9(vram_1_col9), .Col10(vram_1_col10),
    .Col11(vram_1_col11), .Col12(vram_1_col12), .Col13(vram_1_col13), .Col14(vram_1_col14),
    .Col15(vram_1_col15), .Col16(vram_1_col16), .Col17(vram_1_col17), .Col18(vram_1_col18),
    .Col19(vram_1_col19), .Col20(vram_1_col20), .Col21(vram_1_col21), .Col22(vram_1_col22),
    .Col23(vram_1_col23), .Col24(vram_1_col24), .Col25(vram_1_col25), .Col26(vram_1_col26),
    .Col27(vram_1_col27), .Col28(vram_1_col28), .Col29(vram_1_col29), .Col30(vram_1_col30),
    .Col31(vram_1_col31), .Col32(vram_1_col32));  // open: RST
  // BCD_to_7_Segment_decoder bcd_to_7_segment_decoder_1: pin names not known
  // BCD_to_7_Segment_decoder bcd_to_7_segment_decoder_2: pin names not known
  // Binary_to_BCD_converter binary_to_bcd_converter_1: pin names not known; wires that end beside it: Score, binary_to_bcd_converter_1_p2, binary_to_bcd_converter_1_p2, binary_to_bcd_converter_1_p4, binary_to_bcd_converter_1_p4
  Button RESET (.out(RESET_out));
  // BCD_to_7_Segment_decoder bcd_to_7_segment_decoder_3: pin names not known; wires that end beside it: bcd_to_7_segment_decoder_3_p1, bcd_to_7_segment_decoder_3_p1
  RAM #(.addrWidth(5), .dataWidth(9)) ram_1 (
    .addr(AddressBusOut), .we(MemWriteEn), .oe(not_2_out), .clk(CLK_out), .din(DataBusOut), .dout(ram_1_dout));
  not not_2 (not_2_out, MemWriteEn);
  CPU cpu_1 (
    .IOPortInput(portio_1_p3), .DataBusIn(ram_1_dout), .CLK(CLK_out), .RST(RESET_out),
    .ColumnAddress(CurrentAddress),
    .ControlBus({cpu_1_controlbus, MemWriteEn, VRAMHoldEn, ClearScreen, Halt, VRAMWriteEn}),
    .DataBusOut(DataBusOut), .YPosOut(PlayerYPos), .ScoreOut(Score), .AddressBusOut(AddressBusOut),
    .ColumnDataOut(ColumnData));
endmodule

module CPU (
  input  [3:0] IOPortInput,
  input  [8:0] DataBusIn,
  input  CLK,
  input  RST,
  input  [4:0] ColumnAddress,
  output [7:0] ControlBus,
  output [8:0] DataBusOut,
  output [31:0] YPosOut,
  output [8:0] ScoreOut,
  output [4:0] AddressBusOut,
  output [31:0] ColumnDataOut
);

  wire AddressBusSrc, CMPEn, CMPFlagReg_q, ColumnCountEn, comparator_1_eq, comparator_2_eq, d_ff_1_q,
       decoder_1_out0, decoder_1_out1, decoder_1_out2, decoder_1_out3, Jump, LoadInstruction,
       multiplexer_1_out, not_1_out, not_2_out, not_3_out, PCInc, RandEnable, RegWriteEn, Shift_LEFT,
       Shift_RIGHT, t_ff_1_q;
  wire [1:0] RegSelect;
  wire [3:0] Opcode;
  wire [4:0] adder_1_out, Address, multiplexer_2_out, PC_q;
  wire [8:0] controlled_buffer_3_out, RegA_q, RegB_q, Score, undriven, undriven_2;
  wire [31:0] ColumnData, controlled_buffer_1_out, controlled_buffer_2_out, controlled_buffer_4_out,
       controlled_buffer_5_out, multiplexer_3_out, multiplexer_4_out, PlayerYPos, ram_1_dout, shifter_1_out,
       shifter_2_out;

  // NoConnect on decoder_1_out3
  Decoder #(.select(2)) decoder_1 (
    .out0(decoder_1_out0), .out1(decoder_1_out1), .out2(decoder_1_out2), .out3(decoder_1_out3),
    .sel(RegSelect), .en(RegWriteEn));
  Random #(.width(32)) random_1 (.clk(RandEnable), .out(ColumnData));  // open: clr, next
  Register #(.width(9)) IR (.D(DataBusIn), .en(LoadInstruction), .clk(CLK), .Q({Opcode, Address}), .clr(RST));
  Comparator #(.width(5)) comparator_1 (.a(ColumnAddress), .b({5{1'b1}}), .eq(comparator_1_eq));  // open: gt, lt
  Register #(.width(9)) RegA (.D(DataBusIn), .en(decoder_1_out0), .clk(CLK), .Q(RegA_q), .clr(RST));
  Register #(.width(9)) RegB (.D(DataBusIn), .en(decoder_1_out1), .clk(CLK), .Q(RegB_q), .clr(RST));
  Multiplexer multiplexer_1 (.in0(PCInc), .in1(1'b0), .out(multiplexer_1_out), .sel(ControlBus[1]));
  T_Flip_Flop t_ff_1 (.T(1'b1), .clk(comparator_1_eq), .Q(t_ff_1_q));  // open: Qn, reset, preset
  // Probe on Address
  not not_1 (not_1_out, Jump);
  Multiplexer #(.width(5)) multiplexer_2 (.in0(Address), .in1(adder_1_out), .out(multiplexer_2_out), .sel(not_1_out));
  assign controlled_buffer_1_out = comparator_1_eq ? ColumnData : 32'bz;  // Controlled_Buffer controlled_buffer_1
  assign controlled_buffer_2_out = decoder_1_out2 ? PlayerYPos : 32'bz;  // Controlled_Buffer controlled_buffer_2
  Multiplexer #(.width(32)) multiplexer_3 (
    .in0(controlled_buffer_2_out), .in1(32'h10000), .out(multiplexer_3_out), .sel(ControlBus[2]));
  Register #(.width(32)) YPosReg (.D(multiplexer_3_out), .en(decoder_1_out2), .clk(CLK), .Q(YPosOut), .clr(RST));
  Register #(.width(9)) ScoreReg (.D(controlled_buffer_3_out), .en(decoder_1_out2), .clk(CLK), .Q(ScoreOut), .clr(RST));
  assign controlled_buffer_3_out = decoder_1_out2 ? Score : 9'bz;  // Controlled_Buffer controlled_buffer_3
  Register #(.width(5)) PC (.D(multiplexer_2_out), .en(multiplexer_1_out), .clk(CLK), .Q(PC_q), .clr(RST));
  Multiplexer #(.width(32)) multiplexer_4 (
    .in0(ColumnDataOut), .in1(controlled_buffer_1_out), .out(multiplexer_4_out), .sel(comparator_1_eq));
  or or_1 (ControlBus[3], comparator_1_eq, t_ff_1_q);
  // Probe on ram_1_dout
  // NoConnect on undriven
  // NoConnect on undriven_2
  Adder #(.width(5)) adder_1 (.a(5'b00001), .b(PC_q), .out(adder_1_out));  // open: cin, cout
  RAM #(.addrWidth(5), .dataWidth(32)) ram_1 (
    .addr(ColumnAddress), .we(ControlBus[3]), .clk(CLK), .din(multiplexer_4_out), .dout(ram_1_dout));  // open: oe
  Multiplexer #(.select(2), .width(9)) multiplexer_5 (
    .in0(RegA_q), .in1(RegB_q), .in2(undriven), .in3(undriven_2), .out(DataBusOut), .sel(RegSelect));
  Multiplexer #(.width(5)) multiplexer_6 (.in0(Address), .in1(PC_q), .out(AddressBusOut), .sel(not_2_out));
  not not_2 (not_2_out, AddressBusSrc);
  // NoConnect on DataBusOut[8:4]
  Comparator #(.width(4)) comparator_2 (.a(DataBusOut[3:0]), .b(IOPortInput), .eq(comparator_2_eq));  // open: gt, lt
  RAM #(.addrWidth(5), .dataWidth(32)) ram_2 (
    .addr(ColumnAddress), .we(not_3_out), .oe(ControlBus[3]), .clk(CLK), .din(ram_1_dout),
    .dout(ColumnDataOut));
  not not_3 (not_3_out, ControlBus[3]);
  LED led_1 (.in(comparator_2_eq));
  Register #(.width(1)) CMPFlagReg (.D(comparator_2_eq), .clk(CMPEn), .Q(CMPFlagReg_q), .clr(d_ff_1_q));  // open: en
  D_Flip_Flop d_ff_1 (.D(Jump), .clk(CLK), .Q(d_ff_1_q));  // open: Qn, preset, reset
  assign controlled_buffer_4_out = Shift_LEFT ? YPosOut : 32'bz;  // Controlled_Buffer controlled_buffer_4
  assign controlled_buffer_5_out = Shift_RIGHT ? YPosOut : 32'bz;  // Controlled_Buffer controlled_buffer_5
  assign PlayerYPos = Shift_LEFT ? shifter_1_out : 32'bz;  // Controlled_Buffer controlled_buffer_6
  Shifter #(.width(32)) shifter_1 (.in(controlled_buffer_4_out), .\dist (5'b00001), .out(shifter_1_out));
  assign PlayerYPos = Shift_RIGHT ? shifter_2_out : 32'bz;  // Controlled_Buffer controlled_buffer_7
  Shifter #(.shift("lr"), .width(32)) shifter_2 (.in(controlled_buffer_5_out), .\dist (5'b00001), .out(shifter_2_out));
  ControlUnit controlunit_1 (
    .Instruction(Opcode), .CLK(CLK), .RST(RST), .CMPFlag(CMPFlagReg_q), .RegWriteEn(RegWriteEn),
    .RegSelect(RegSelect), .LoadInstruction(LoadInstruction), .Jump(Jump), .PCInc(PCInc),
    .Halt(ControlBus[1]), .AddressBusSrc(AddressBusSrc), .ColumnCounterEn(ColumnCountEn), .CMPEn(CMPEn),
    .Shift_LEFT(Shift_LEFT), .Shift_RIGHT(Shift_RIGHT), .RandEnable(RandEnable), .ClearScreen(ControlBus[2]),
    .VRAMWriteEn(ControlBus[0]), .MemWriteEn(ControlBus[4]));

  // Other names for the same wires on the sheet: VRAMWriteEn = ControlBus[0]; Halt = ControlBus[1];
  //   ClearScreen = ControlBus[2]; VRAMHoldEn = ControlBus[3]; MemWriteEn = ControlBus[4]
endmodule

module NextStateLogic (
  input  [4:0] CurrentState,
  input  [3:0] Instruction,
  output [4:0] NextState
);

  wire and_1_out, and_2_out, and_3_out, and_4_out, and_6_out, and_7_out, and_8_out, and_9_out, not_1_out,
       not_2_out, not_3_out, not_4_out, not_5_out;

  not not_1 (not_1_out, CurrentState[4]);
  not not_2 (not_2_out, CurrentState[3]);
  not not_3 (not_3_out, CurrentState[2]);
  not not_4 (not_4_out, CurrentState[1]);
  not not_5 (not_5_out, CurrentState[0]);
  and and_1 (and_1_out, CurrentState[4], CurrentState[3], not_3_out, not_4_out, not_5_out);
  and and_2 (and_2_out, not_1_out, not_2_out, not_3_out, CurrentState[1], not_5_out);
  and and_3 (and_3_out, CurrentState[4], CurrentState[3], not_3_out, not_4_out, not_5_out);
  and and_4 (and_4_out, not_1_out, not_2_out, not_3_out, CurrentState[1], not_5_out, Instruction[3]);
  and and_5 (NextState[2], not_1_out, not_2_out, not_3_out, CurrentState[1], not_5_out, Instruction[2]);
  and and_6 (and_6_out, not_1_out, not_2_out, not_3_out, CurrentState[1], not_5_out, Instruction[1]);
  and and_7 (and_7_out, not_1_out, not_2_out, not_3_out, not_4_out, CurrentState[0]);
  and and_8 (and_8_out, not_1_out, not_2_out, not_3_out, not_4_out, not_5_out);
  and and_9 (and_9_out, not_1_out, not_2_out, not_3_out, not_5_out, Instruction[0]);
  or or_1 (NextState[4], and_1_out, and_2_out);
  or or_2 (NextState[3], and_3_out, and_4_out);
  or or_3 (NextState[1], and_6_out, and_7_out);
  or or_4 (NextState[0], and_8_out, and_9_out);
endmodule

module OutputLogic (
  input  CMPFlag,
  input  [4:0] CurrentState,
  output RegWriteEn,
  output [1:0] RegSelect,
  output LoadInstruction,
  output Jump,
  output PCInc,
  output Halt,
  output AddressBusSrc,
  output ColumnCountEn,
  output CMPEn,
  output Shift_Left,
  output Shift_Right,
  output RandEnable,
  output ClearScreen,
  output VRAMWriteEn,
  output MemWriteEn
);

  wire and_1_out, and_2_out, and_3_out, and_4_out, and_5_out, and_7_out, and_8_out, and_9_out, and_10_out,
       and_19_out, and_20_out, not_1_out, not_2_out, not_3_out, not_4_out, not_5_out;

  not not_1 (not_1_out, CurrentState[4]);
  not not_2 (not_2_out, CurrentState[3]);
  not not_3 (not_3_out, CurrentState[2]);
  not not_4 (not_4_out, CurrentState[1]);
  not not_5 (not_5_out, CurrentState[0]);
  and and_1 (and_1_out, CurrentState[4], CurrentState[2], CurrentState[1], not_5_out);
  and and_2 (and_2_out, CurrentState[4], CurrentState[3], not_3_out, CurrentState[0]);
  or or_1 (RegWriteEn, and_1_out, and_2_out, and_3_out);
  and and_3 (and_3_out, CurrentState[4], CurrentState[3], not_3_out, CurrentState[1]);
  and and_4 (and_4_out, CurrentState[4], CurrentState[3], not_3_out, not_4_out, CurrentState[0]);
  or or_2 (RegSelect[1], and_4_out, and_5_out);
  and and_5 (and_5_out, CurrentState[4], CurrentState[3], CurrentState[1], not_5_out);
  and and_6 (LoadInstruction, not_1_out, not_2_out, not_3_out, not_4_out, CurrentState[0]);
  and and_7 (and_7_out, CurrentState[4], not_2_out, not_3_out, not_4_out, CurrentState[0]);
  or or_3 (Jump, and_7_out, and_8_out);
  and and_8 (and_8_out, CMPFlag, CurrentState[4], not_2_out, not_3_out, CurrentState[1], not_5_out);
  and and_9 (and_9_out, not_2_out, not_3_out, not_4_out, CurrentState[0]);
  or or_4 (PCInc, and_9_out, and_10_out);
  and and_10 (and_10_out, CurrentState[4], not_2_out, not_3_out, CurrentState[1], not_5_out);
  and and_11 (Halt, CurrentState[4], CurrentState[3], not_3_out, not_4_out, not_5_out);
  and and_12 (AddressBusSrc, not_1_out, not_2_out, not_3_out, CurrentState[1], not_5_out);
  and and_13 (ColumnCountEn, CurrentState[4], CurrentState[3], CurrentState[2]);
  and and_14 (CMPEn, CurrentState[4], not_2_out, CurrentState[2], not_4_out, not_5_out);
  and and_15 (Shift_Left, CurrentState[4], CurrentState[3], not_3_out, CurrentState[1], not_5_out);
  and and_16 (Shift_Right, CurrentState[4], CurrentState[3], not_3_out, not_4_out, CurrentState[0]);
  and and_17 (RandEnable, CurrentState[4], CurrentState[3], CurrentState[2], not_4_out, not_5_out);
  and and_18 (ClearScreen, CurrentState[4], CurrentState[3], CurrentState[2], CurrentState[1], not_5_out);
  and and_19 (and_19_out, CurrentState[4], CurrentState[3], CurrentState[1], CurrentState[0]);
  or or_5 (VRAMWriteEn, and_19_out, and_20_out);
  and and_20 (and_20_out, CurrentState[4], CurrentState[3], CurrentState[2]);
  and and_21 (MemWriteEn, CurrentState[4], not_2_out, not_3_out, CurrentState[1], CurrentState[0]);

  assign RegSelect[0] = 1'b0;
endmodule

module DisplayRegFile (
  input  [31:0] DataBus,
  input  [4:0] AddressBus,
  input  CLK,
  input  RST,
  output [31:0] RegOut1,
  output [31:0] RegOut2,
  output [31:0] RegOut3,
  output [31:0] RegOut4,
  output [31:0] RegOut5,
  output [31:0] RegOut6,
  output [31:0] RegOut7,
  output [31:0] RegOut8,
  output [31:0] RegOut9,
  output [31:0] RegOut10,
  output [31:0] RegOut11,
  output [31:0] RegOut12,
  output [31:0] RegOut13,
  output [31:0] RegOut14,
  output [31:0] RegOut15,
  output [31:0] RegOut16,
  output [31:0] RegOut17,
  output [31:0] RegOut18,
  output [31:0] RegOut19,
  output [31:0] RegOut20,
  output [31:0] RegOut21,
  output [31:0] RegOut22,
  output [31:0] RegOut23,
  output [31:0] RegOut24,
  output [31:0] RegOut25,
  output [31:0] RegOut26,
  output [31:0] RegOut27,
  output [31:0] RegOut28,
  output [31:0] RegOut29,
  output [31:0] RegOut30,
  output [31:0] RegOut31,
  output [31:0] RegOut32
);

  wire demultiplexer_2_out0, demultiplexer_2_out1, demultiplexer_2_out2, demultiplexer_2_out3,
       demultiplexer_2_out4, demultiplexer_2_out5, demultiplexer_2_out6, demultiplexer_2_out7,
       demultiplexer_2_out8, demultiplexer_2_out9, demultiplexer_2_out10, demultiplexer_2_out11,
       demultiplexer_2_out12, demultiplexer_2_out13, demultiplexer_2_out14, demultiplexer_2_out15,
       demultiplexer_2_out16, demultiplexer_2_out17, demultiplexer_2_out18, demultiplexer_2_out19,
       demultiplexer_2_out20, demultiplexer_2_out21, demultiplexer_2_out22, demultiplexer_2_out23,
       demultiplexer_2_out24, demultiplexer_2_out25, demultiplexer_2_out26, demultiplexer_2_out27,
       demultiplexer_2_out28, demultiplexer_2_out29, demultiplexer_2_out30, demultiplexer_2_out31;
  wire [31:0] demultiplexer_1_out0, demultiplexer_1_out1, demultiplexer_1_out2, demultiplexer_1_out3,
       demultiplexer_1_out4, demultiplexer_1_out5, demultiplexer_1_out6, demultiplexer_1_out7,
       demultiplexer_1_out8, demultiplexer_1_out9, demultiplexer_1_out10, demultiplexer_1_out11,
       demultiplexer_1_out12, demultiplexer_1_out13, demultiplexer_1_out14, demultiplexer_1_out15,
       demultiplexer_1_out16, demultiplexer_1_out17, demultiplexer_1_out18, demultiplexer_1_out19,
       demultiplexer_1_out20, demultiplexer_1_out21, demultiplexer_1_out22, demultiplexer_1_out23,
       demultiplexer_1_out24, demultiplexer_1_out25, demultiplexer_1_out26, demultiplexer_1_out27,
       demultiplexer_1_out28, demultiplexer_1_out29, demultiplexer_1_out30, demultiplexer_1_out31;

  Demultiplexer #(.select(5), .width(32)) demultiplexer_1 (
    .out0(demultiplexer_1_out0), .out1(demultiplexer_1_out1), .out2(demultiplexer_1_out2),
    .out3(demultiplexer_1_out3), .out4(demultiplexer_1_out4), .out5(demultiplexer_1_out5),
    .out6(demultiplexer_1_out6), .out7(demultiplexer_1_out7), .out8(demultiplexer_1_out8),
    .out9(demultiplexer_1_out9), .out10(demultiplexer_1_out10), .out11(demultiplexer_1_out11),
    .out12(demultiplexer_1_out12), .out13(demultiplexer_1_out13), .out14(demultiplexer_1_out14),
    .out15(demultiplexer_1_out15), .out16(demultiplexer_1_out16), .out17(demultiplexer_1_out17),
    .out18(demultiplexer_1_out18), .out19(demultiplexer_1_out19), .out20(demultiplexer_1_out20),
    .out21(demultiplexer_1_out21), .out22(demultiplexer_1_out22), .out23(demultiplexer_1_out23),
    .out24(demultiplexer_1_out24), .out25(demultiplexer_1_out25), .out26(demultiplexer_1_out26),
    .out27(demultiplexer_1_out27), .out28(demultiplexer_1_out28), .out29(demultiplexer_1_out29),
    .out30(demultiplexer_1_out30), .out31(demultiplexer_1_out31), .in(DataBus), .sel(AddressBus));
  Demultiplexer #(.select(5)) demultiplexer_2 (
    .out0(demultiplexer_2_out0), .out1(demultiplexer_2_out1), .out2(demultiplexer_2_out2),
    .out3(demultiplexer_2_out3), .out4(demultiplexer_2_out4), .out5(demultiplexer_2_out5),
    .out6(demultiplexer_2_out6), .out7(demultiplexer_2_out7), .out8(demultiplexer_2_out8),
    .out9(demultiplexer_2_out9), .out10(demultiplexer_2_out10), .out11(demultiplexer_2_out11),
    .out12(demultiplexer_2_out12), .out13(demultiplexer_2_out13), .out14(demultiplexer_2_out14),
    .out15(demultiplexer_2_out15), .out16(demultiplexer_2_out16), .out17(demultiplexer_2_out17),
    .out18(demultiplexer_2_out18), .out19(demultiplexer_2_out19), .out20(demultiplexer_2_out20),
    .out21(demultiplexer_2_out21), .out22(demultiplexer_2_out22), .out23(demultiplexer_2_out23),
    .out24(demultiplexer_2_out24), .out25(demultiplexer_2_out25), .out26(demultiplexer_2_out26),
    .out27(demultiplexer_2_out27), .out28(demultiplexer_2_out28), .out29(demultiplexer_2_out29),
    .out30(demultiplexer_2_out30), .out31(demultiplexer_2_out31), .sel(AddressBus));  // open: in
  Register #(.width(32)) register_1 (
    .D(demultiplexer_1_out0), .en(demultiplexer_2_out0), .clk(CLK), .Q(RegOut1), .clr(RST));
  Register #(.width(32)) register_2 (
    .D(demultiplexer_1_out8), .en(demultiplexer_2_out8), .clk(CLK), .Q(RegOut9), .clr(RST));
  Register #(.width(32)) register_3 (
    .D(demultiplexer_1_out16), .en(demultiplexer_2_out16), .clk(CLK), .Q(RegOut17), .clr(RST));
  Register #(.width(32)) register_4 (
    .D(demultiplexer_1_out24), .en(demultiplexer_2_out24), .clk(CLK), .Q(RegOut25), .clr(RST));
  Register #(.width(32)) register_5 (
    .D(demultiplexer_1_out1), .en(demultiplexer_2_out1), .clk(CLK), .Q(RegOut2), .clr(RST));
  Register #(.width(32)) register_6 (
    .D(demultiplexer_1_out9), .en(demultiplexer_2_out9), .clk(CLK), .Q(RegOut10), .clr(RST));
  Register #(.width(32)) register_7 (
    .D(demultiplexer_1_out17), .en(demultiplexer_2_out17), .clk(CLK), .Q(RegOut18), .clr(RST));
  Register #(.width(32)) register_8 (
    .D(demultiplexer_1_out25), .en(demultiplexer_2_out25), .clk(CLK), .Q(RegOut26), .clr(RST));
  Register #(.width(32)) register_9 (
    .D(demultiplexer_1_out2), .en(demultiplexer_2_out2), .clk(CLK), .Q(RegOut3), .clr(RST));
  Register #(.width(32)) register_10 (
    .D(demultiplexer_1_out10), .en(demultiplexer_2_out10), .clk(CLK), .Q(RegOut11), .clr(RST));
  Register #(.width(32)) register_11 (
    .D(demultiplexer_1_out18), .en(demultiplexer_2_out18), .clk(CLK), .Q(RegOut19), .clr(RST));
  Register #(.width(32)) register_12 (
    .D(demultiplexer_1_out26), .en(demultiplexer_2_out26), .clk(CLK), .Q(RegOut27), .clr(RST));
  Register #(.width(32)) register_13 (
    .D(demultiplexer_1_out3), .en(demultiplexer_2_out3), .clk(CLK), .Q(RegOut4), .clr(RST));
  Register #(.width(32)) register_14 (
    .D(demultiplexer_1_out11), .en(demultiplexer_2_out11), .clk(CLK), .Q(RegOut12), .clr(RST));
  Register #(.width(32)) register_15 (
    .D(demultiplexer_1_out19), .en(demultiplexer_2_out19), .clk(CLK), .Q(RegOut20), .clr(RST));
  Register #(.width(32)) register_16 (
    .D(demultiplexer_1_out27), .en(demultiplexer_2_out27), .clk(CLK), .Q(RegOut28), .clr(RST));
  Register #(.width(32)) register_17 (
    .D(demultiplexer_1_out4), .en(demultiplexer_2_out4), .clk(CLK), .Q(RegOut5), .clr(RST));
  Register #(.width(32)) register_18 (
    .D(demultiplexer_1_out12), .en(demultiplexer_2_out12), .clk(CLK), .Q(RegOut13), .clr(RST));
  Register #(.width(32)) register_19 (
    .D(demultiplexer_1_out20), .en(demultiplexer_2_out20), .clk(CLK), .Q(RegOut21), .clr(RST));
  Register #(.width(32)) register_20 (
    .D(demultiplexer_1_out28), .en(demultiplexer_2_out28), .clk(CLK), .Q(RegOut29), .clr(RST));
  Register #(.width(32)) register_21 (
    .D(demultiplexer_1_out5), .en(demultiplexer_2_out5), .clk(CLK), .Q(RegOut6), .clr(RST));
  Register #(.width(32)) register_22 (
    .D(demultiplexer_1_out13), .en(demultiplexer_2_out13), .clk(CLK), .Q(RegOut14), .clr(RST));
  Register #(.width(32)) register_23 (
    .D(demultiplexer_1_out21), .en(demultiplexer_2_out21), .clk(CLK), .Q(RegOut22), .clr(RST));
  Register #(.width(32)) register_24 (
    .D(demultiplexer_1_out29), .en(demultiplexer_2_out29), .clk(CLK), .Q(RegOut30), .clr(RST));
  Register #(.width(32)) register_25 (
    .D(demultiplexer_1_out6), .en(demultiplexer_2_out6), .clk(CLK), .Q(RegOut7), .clr(RST));
  Register #(.width(32)) register_26 (
    .D(demultiplexer_1_out14), .en(demultiplexer_2_out14), .clk(CLK), .Q(RegOut15), .clr(RST));
  Register #(.width(32)) register_27 (
    .D(demultiplexer_1_out22), .en(demultiplexer_2_out22), .clk(CLK), .Q(RegOut23), .clr(RST));
  Register #(.width(32)) register_28 (
    .D(demultiplexer_1_out30), .en(demultiplexer_2_out30), .clk(CLK), .Q(RegOut31), .clr(RST));
  Register #(.width(32)) register_29 (
    .D(demultiplexer_1_out7), .en(demultiplexer_2_out7), .clk(CLK), .Q(RegOut8), .clr(RST));
  Register #(.width(32)) register_30 (
    .D(demultiplexer_1_out15), .en(demultiplexer_2_out15), .clk(CLK), .Q(RegOut16), .clr(RST));
  Register #(.width(32)) register_31 (
    .D(demultiplexer_1_out23), .en(demultiplexer_2_out23), .clk(CLK), .Q(RegOut24), .clr(RST));
  Register #(.width(32)) register_32 (
    .D(demultiplexer_1_out31), .en(demultiplexer_2_out31), .clk(CLK), .Q(RegOut32), .clr(RST));
endmodule

module VRAM (
  input  [4:0] AddressBus,
  input  [31:0] VRAMDataBus,
  input  WriteEnable,
  input  CLK,
  input  RST,
  output [31:0] Col1,
  output [31:0] Col2,
  output [31:0] Col3,
  output [31:0] Col4,
  output [31:0] Col5,
  output [31:0] Col6,
  output [31:0] Col7,
  output [31:0] Col8,
  output [31:0] Col9,
  output [31:0] Col10,
  output [31:0] Col11,
  output [31:0] Col12,
  output [31:0] Col13,
  output [31:0] Col14,
  output [31:0] Col15,
  output [31:0] Col16,
  output [31:0] Col17,
  output [31:0] Col18,
  output [31:0] Col19,
  output [31:0] Col20,
  output [31:0] Col21,
  output [31:0] Col22,
  output [31:0] Col23,
  output [31:0] Col24,
  output [31:0] Col25,
  output [31:0] Col26,
  output [31:0] Col27,
  output [31:0] Col28,
  output [31:0] Col29,
  output [31:0] Col30,
  output [31:0] Col31,
  output [31:0] Col32
);

  wire d_ff_1_q;
  wire [4:0] register_1_q;
  wire [31:0] ram_1_dout;

  D_Flip_Flop d_ff_1 (.D(WriteEnable), .clk(CLK), .Q(d_ff_1_q));  // open: Qn, preset, reset
  RAM #(.addrWidth(5), .dataWidth(32)) ram_1 (
    .addr(AddressBus), .we(d_ff_1_q), .clk(CLK), .din(VRAMDataBus), .dout(ram_1_dout));  // open: oe
  Register #(.width(5)) register_1 (.D(AddressBus), .clk(CLK), .Q(register_1_q));  // open: en, clr
  // Probe on ram_1_dout
  DisplayRegFile displayregfile_1 (
    .DataBus(ram_1_dout), .AddressBus(register_1_q), .CLK(CLK), .RST(RST), .RegOut1(Col1), .RegOut2(Col2),
    .RegOut3(Col3), .RegOut4(Col4), .RegOut5(Col5), .RegOut6(Col6), .RegOut7(Col7), .RegOut8(Col8),
    .RegOut9(Col9), .RegOut10(Col10), .RegOut11(Col11), .RegOut12(Col12), .RegOut13(Col13), .RegOut14(Col14),
    .RegOut15(Col15), .RegOut16(Col16), .RegOut17(Col17), .RegOut18(Col18), .RegOut19(Col19),
    .RegOut20(Col20), .RegOut21(Col21), .RegOut22(Col22), .RegOut23(Col23), .RegOut24(Col24),
    .RegOut25(Col25), .RegOut26(Col26), .RegOut27(Col27), .RegOut28(Col28), .RegOut29(Col29),
    .RegOut30(Col30), .RegOut31(Col31), .RegOut32(Col32));
endmodule

module ControlUnit (
  input  [3:0] Instruction,
  input  CLK,
  input  RST,
  input  CMPFlag,
  output RegWriteEn,
  output [1:0] RegSelect,
  output LoadInstruction,
  output Jump,
  output PCInc,
  output Halt,
  output AddressBusSrc,
  output ColumnCounterEn,
  output CMPEn,
  output Shift_LEFT,
  output Shift_RIGHT,
  output RandEnable,
  output ClearScreen,
  output VRAMWriteEn,
  output MemWriteEn
);

  wire [4:0] nextstatelogic_1_nextstate, register_1_q;

  NextStateLogic nextstatelogic_1 (
    .CurrentState(register_1_q), .Instruction(Instruction), .NextState(nextstatelogic_1_nextstate));
  Register #(.width(5)) register_1 (.D(nextstatelogic_1_nextstate), .en(1'b1), .clk(CLK), .Q(register_1_q), .clr(RST));
  OutputLogic outputlogic_1 (
    .CMPFlag(CMPFlag), .CurrentState(register_1_q), .RegWriteEn(RegWriteEn), .RegSelect(RegSelect),
    .LoadInstruction(LoadInstruction), .Jump(Jump), .PCInc(PCInc), .Halt(Halt),
    .AddressBusSrc(AddressBusSrc), .ColumnCountEn(ColumnCounterEn), .CMPEn(CMPEn), .Shift_Left(Shift_LEFT),
    .Shift_Right(Shift_RIGHT), .RandEnable(RandEnable), .ClearScreen(ClearScreen), .VRAMWriteEn(VRAMWriteEn),
    .MemWriteEn(MemWriteEn));
endmodule
